# Fritzing sketch transmitter (saved by Fritzing 0.8.0b)
breadboards: 1

parts:
  Part1 = Arduino Leonardo (Rev3b)
  Q2 = NPN-Transistor [package="SOT-23 [SMD]"]
  LED1 = LED - 3mm [color="Red (633nm)" package="3 mm [THT]"]
  R1 = Photocell (LDR) [package=THT]

nets:
  N1: Part1.D2/SDA, Q2.0
  N2: Part1.D4/A6, Part1.A0, R1.pin_1
  N3: Part1.3V3, Q2.2
  N4: Part1.GND, LED1.cathode, R1.pin_0
  N5: Q2.1, LED1.anode
